// Logisim project CPU_Design.circ as structural Verilog: 4 circuits, main circuit main
module main (
  input  [15:0] in_1,
  output [7:0] Result,
  output [3:0] Func,
  output [5:0] ImmediateValue,
  output [7:0] ExtendedImm,
  output [7:0] out_6,
  output [7:0] out_7,
  output [7:0] out_8,
  output [7:0] out_9,
  output [5:0] OPCODE
);

  wire clock_1_out, controlunit_1_alusource, controlunit_1_registerdest, controlunit_1_writeenable;
  wire [1:0] multiplexer_1_out;
  wire [2:0] controlunit_1_alucontrol;
  wire [7:0] multiplexer_2_out, registerfile_1_rd1, registerfile_1_rd2;

  assign ExtendedImm = {{2{in_1[5]}}, in_1[5:0]};  // Bit_Extender bit_extender_1
  Clock clock_1 (.out(clock_1_out));
  Multiplexer #(.width(2)) multiplexer_1 (
    .in0(in_1[5:4]), .in1(in_1[7:6]), .out(multiplexer_1_out), .sel(controlunit_1_registerdest));
  ControlUnit controlunit_1 (
    .OpCode(in_1[15:10]), .Func(in_1[3:0]), .RegisterDest(controlunit_1_registerdest),
    .ALUSource(controlunit_1_alusource), .WriteEnable(controlunit_1_writeenable),
    .ALUControl(controlunit_1_alucontrol));
  Multiplexer #(.width(8)) multiplexer_2 (
    .in0(registerfile_1_rd2), .in1(ExtendedImm), .out(multiplexer_2_out), .sel(controlunit_1_alusource));
  RegisterFile registerfile_1 (
    .A1(in_1[9:8]), .A2(in_1[7:6]), .WriteData3(Result), .Clock(clock_1_out),
    .WriteEnable(controlunit_1_writeenable), .A3(multiplexer_1_out), .RegisterADisplay(out_6),
    .RD1(registerfile_1_rd1), .RegisterBDisplay(out_7), .RegisterCDisplay(out_8), .RD2(registerfile_1_rd2),
    .RegisterDDisplay(out_9));
  ALU alu_1 (
    .SrcA(registerfile_1_rd1), .SrcB(multiplexer_2_out), .AluSelect(controlunit_1_alucontrol), .Result(Result));

  assign Func = in_1[3:0];
  assign ImmediateValue = in_1[5:0];
  assign OPCODE = in_1[15:10];
endmodule

module RegisterFile (
  input  [1:0] A1,
  input  [1:0] A2,
  input  [7:0] WriteData3,
  input  Clock,
  input  WriteEnable,
  input  [1:0] A3,
  output [7:0] RegisterADisplay,
  output [7:0] RD1,
  output [7:0] RegisterBDisplay,
  output [7:0] RegisterCDisplay,
  output [7:0] RD2,
  output [7:0] RegisterDDisplay
);

  wire and_1_out, and_2_out, and_3_out, and_4_out, decoder_1_out0, decoder_1_out1, decoder_1_out2,
       decoder_1_out3;

  Decoder #(.select(2)) decoder_1 (
    .out0(decoder_1_out0), .out1(decoder_1_out1), .out2(decoder_1_out2), .out3(decoder_1_out3), .sel(A3));  // open: en
  and and_1 (and_1_out, WriteEnable, decoder_1_out0);
  and and_2 (and_2_out, WriteEnable, decoder_1_out1);
  and and_3 (and_3_out, WriteEnable, decoder_1_out2);
  and and_4 (and_4_out, WriteEnable, decoder_1_out3);
  Register RegisterA (.D(WriteData3), .en(and_1_out), .clk(Clock), .Q(RegisterADisplay));  // open: clr
  Register RegisterB (.D(WriteData3), .en(and_2_out), .clk(Clock), .Q(RegisterBDisplay));  // open: clr
  Register RegisterC (.D(WriteData3), .en(and_3_out), .clk(Clock), .Q(RegisterCDisplay));  // open: clr
  Register RegisterD (.D(WriteData3), .en(and_4_out), .clk(Clock), .Q(RegisterDDisplay));  // open: clr
  Multiplexer #(.select(2), .width(8)) multiplexer_1 (
    .in0(RegisterADisplay), .in1(RegisterBDisplay), .in2(RegisterCDisplay), .in3(RegisterDDisplay),
    .out(RD1), .sel(A1));
  Multiplexer #(.select(2), .width(8)) multiplexer_2 (
    .in0(RegisterADisplay), .in1(RegisterBDisplay), .in2(RegisterCDisplay), .in3(RegisterDDisplay),
    .out(RD2), .sel(A2));
endmodule

module ALU (
  input  [7:0] SrcA,
  input  [7:0] SrcB,
  input  [2:0] AluSelect,
  output [7:0] Result
);

  wire [7:0] adder_1_out, and_1_out, multiplexer_1_out, not_1_out, or_1_out;

  assign not_1_out = ~SrcB;  // NOT_Gate not_1, 8 bits wide
  Multiplexer #(.width(8)) multiplexer_1 (.in0(SrcB), .in1(not_1_out), .out(multiplexer_1_out), .sel(AluSelect[2]));
  assign and_1_out = SrcA & multiplexer_1_out;  // AND_Gate and_1, 8 bits wide
  assign or_1_out = SrcA | multiplexer_1_out;  // OR_Gate or_1, 8 bits wide
  Adder adder_1 (.a(SrcA), .b(multiplexer_1_out), .out(adder_1_out));  // open: cin, cout
  Multiplexer #(.select(2), .width(8)) multiplexer_2 (
    .in0(and_1_out), .in1(or_1_out), .in2(adder_1_out), .out(Result), .sel(AluSelect[1:0]));  // open: in3
endmodule

module ControlUnit (
  input  [5:0] OpCode,
  input  [3:0] Func,
  output RegisterDest,
  output ALUSource,
  output WriteEnable,
  output [2:0] ALUControl
);

  wire decoder_1_out0, decoder_1_out1, decoder_1_out2, not_1_out, or_1_out;

  Decoder #(.select(2)) decoder_1 (
    .out0(decoder_1_out0), .out1(decoder_1_out1), .out2(decoder_1_out2), .sel(OpCode[1:0]));  // open: out3, en
  not not_1 (not_1_out, decoder_1_out0);
  Multiplexer #(.select(2), .width(3)) multiplexer_1 (
    .in0(Func[2:0]), .in1(3'b010), .in2(3'b110), .out(ALUControl), .sel(OpCode[1:0]));  // open: in3
  or or_1 (or_1_out, not_1_out, decoder_1_out1, decoder_1_out2);
  Multiplexer multiplexer_2 (.in0(1'b0), .in1(1'b1), .out(ALUSource), .sel(or_1_out));

  assign RegisterDest = ALUSource;
  assign WriteEnable = 1'b1;

  // Notes on the sheet:
  //   Func Codes need to be adjusted to match alu logic
endmodule
